# Fritzing sketch kunto (saved by Fritzing 0.9.3b)
breadboards: 1

parts:
  パーツ1 = Arduino Uno (Rev3)
  IC2 = DIP - 20 pins [chip_label=IC package="DIP (Dual Inline) [THT]"]
  R1 = Resistor [tolerance=±5% resistance=500 package=THT]
  IC3 = KXSC7-2050 [chip_label=IC]
  IC4 = DIP - 8 pins [chip_label=IC package="DIP (Dual Inline) [THT]"]
  R2 = Resistor [tolerance=±5% resistance=1k package=THT]

nets:
  N1: パーツ1.A0, IC3.connector4
  N2: パーツ1.A1, IC3.connector5
  N3: パーツ1.A2, IC3.connector6
  N4: パーツ1.A4/SDA, IC4.pin2
  N5: パーツ1.A5/SCL, IC4.pin3
  N6: パーツ1.D10_PWM/SS, IC2.pin2
  N7: パーツ1.D11_PWM/MOSI, R1.Pin_0
  N8: パーツ1.3V3, IC2.pin1, IC3.connector0, IC3.connector1, IC4.pin1
  N9: パーツ1.GND, IC2.pin10, IC3.connector7, IC4.pin4, R2.Pin_1
  N10: IC2.pin3, R1.Pin_1, R2.Pin_0

custom parts:
  DIP - 20 pins: A DIP stand-in part for whatever IC you want. With 20 pins on a 300mil dual inline package (DIP) footprint.
  DIP - 8 pins: A DIP stand-in part for whatever IC you want. With 8 pins on a 300mil dual inline package (DIP) footprint.
